// Logisim project 231_project_decoder.circ as structural Verilog: 1 circuit, main circuit main
module main (
  input  X,
  input  Y,
  input  Z
);

  wire decoder_1_out0, decoder_1_out1, decoder_1_out2, decoder_1_out3, decoder_1_out4, decoder_1_out5,
       decoder_1_out6, decoder_1_out7, or_1_out, or_2_out, or_3_out, or_4_out, or_5_out, or_6_out, or_7_out,
       or_8_out;

  Decoder #(.select(3)) decoder_1 (
    .out0(decoder_1_out0), .out1(decoder_1_out1), .out2(decoder_1_out2), .out3(decoder_1_out3),
    .out4(decoder_1_out4), .out5(decoder_1_out5), .out6(decoder_1_out6), .out7(decoder_1_out7),
    .sel({X, Y, Z}), .en(1'b1));
  or or_1 (or_1_out, decoder_1_out0, decoder_1_out1, decoder_1_out2, decoder_1_out3, decoder_1_out4);
  or or_2 (or_2_out, decoder_1_out0, decoder_1_out1, decoder_1_out2, decoder_1_out3, decoder_1_out4);
  or or_3 (or_3_out, decoder_1_out0, decoder_1_out2, decoder_1_out3, decoder_1_out0);
  or or_4 (or_4_out, decoder_1_out1, decoder_1_out2, decoder_1_out3, decoder_1_out4, decoder_1_out6);
  or or_5 (or_5_out, or_1_out, decoder_1_out7);
  or or_6 (or_6_out, decoder_1_out3, decoder_1_out5, decoder_1_out4, decoder_1_out7);
  or or_7 (or_7_out, decoder_1_out1, decoder_1_out4, decoder_1_out5, decoder_1_out7);
  or or_8 (or_8_out, decoder_1_out0, decoder_1_out1, decoder_1_out2);
  _7_Segment_Display u_7_segment_display_1 (
    .g(or_4_out), .f(or_8_out), .a(or_5_out), .b(or_6_out), .e(or_3_out), .d(or_2_out), .c(or_7_out));  // open: dp

  // Notes on the sheet:
  //   CSE 231 Section 1Group 7 Fall 2017
endmodule
