// Logisim project 231_sequential.circ as structural Verilog: 1 circuit, main circuit main
module main (
  input  Input_A,
  output B,
  output out_3,
  output out_4,
  output out_5
);

  wire and_1_out, and_2_out, and_3_out, and_4_out, and_5_out, and_6_out, and_7_out, and_8_out, and_9_out,
       and_10_out, and_11_out, button_1_out, decoder_1_out0, decoder_1_out1, decoder_1_out2, decoder_1_out3,
       decoder_1_out4, decoder_1_out5, decoder_1_out6, decoder_1_out7, not_1_out, not_2_out, not_3_out,
       not_4_out, not_5_out, or_1_out, or_2_out, or_3_out, or_4_out, or_5_out, or_6_out, or_7_out, or_8_out,
       or_9_out, or_10_out, or_11_out, or_12_out, or_13_out;

  not not_1 (not_1_out, Input_A);
  not not_2 (not_2_out, B);
  not not_3 (not_3_out, out_3);
  not not_4 (not_4_out, out_5);
  not not_5 (not_5_out, out_4);
  and and_1 (and_1_out, Input_A, out_3, out_4, not_4_out);
  and and_2 (and_2_out, not_1_out, out_3, out_4, out_5);
  and and_3 (and_3_out, Input_A, not_4_out);
  and and_4 (and_4_out, not_1_out, not_5_out, not_5_out);
  and and_5 (and_5_out, Input_A, out_4, out_5);
  and and_6 (and_6_out, not_1_out, not_5_out, not_4_out);
  and and_7 (and_7_out, Input_A, out_5);
  and and_8 (and_8_out, not_1_out, not_4_out);
  and and_9 (and_9_out, Input_A, out_5);
  and and_10 (and_10_out, not_1_out, not_4_out);
  and and_11 (and_11_out, Input_A, not_2_out, out_3);
  or or_1 (or_1_out, and_1_out, and_2_out);
  or or_2 (or_2_out, and_3_out, and_4_out);
  or or_3 (or_3_out, and_5_out, and_6_out);
  or or_4 (or_4_out, B, and_7_out, and_8_out);
  or or_5 (or_5_out, and_9_out, and_10_out, and_11_out);
  J_K_Flip_Flop j_k_ff_1 (.J(or_1_out), .clk(button_1_out), .K(or_2_out), .Q(B));  // open: Qn, preset, en, reset
  J_K_Flip_Flop j_k_ff_2 (.J(or_3_out), .clk(button_1_out), .K(or_3_out), .Q(out_3));  // open: Qn, preset, en, reset
  J_K_Flip_Flop j_k_ff_3 (.J(or_4_out), .clk(button_1_out), .K(or_5_out), .Q(out_4));  // open: Qn, preset, en, reset
  J_K_Flip_Flop j_k_ff_4 (.J(1'b1), .clk(button_1_out), .K(1'b1), .Q(out_5));  // open: Qn, preset, en, reset
  Button button_1 (.out(button_1_out));
  Decoder #(.select(3)) decoder_1 (
    .out0(decoder_1_out0), .out1(decoder_1_out1), .out2(decoder_1_out2), .out3(decoder_1_out3),
    .out4(decoder_1_out4), .out5(decoder_1_out5), .out6(decoder_1_out6), .out7(decoder_1_out7),
    .sel({out_3, out_4, out_5}), .en(1'b1));
  or or_6 (or_6_out, decoder_1_out0, decoder_1_out1, decoder_1_out2, decoder_1_out3, decoder_1_out4);
  or or_7 (or_7_out, decoder_1_out0, decoder_1_out1, decoder_1_out2, decoder_1_out3, decoder_1_out4);
  or or_8 (or_8_out, decoder_1_out0, decoder_1_out2, decoder_1_out3, decoder_1_out0);
  or or_9 (or_9_out, decoder_1_out1, decoder_1_out2, decoder_1_out3, decoder_1_out4, decoder_1_out6);
  or or_10 (or_10_out, decoder_1_out0, decoder_1_out1, decoder_1_out2);
  or or_11 (or_11_out, or_6_out, decoder_1_out7);
  or or_12 (or_12_out, decoder_1_out3, decoder_1_out5, decoder_1_out4, decoder_1_out7);
  or or_13 (or_13_out, decoder_1_out1, decoder_1_out4, decoder_1_out5, decoder_1_out7);
  _7_Segment_Display u_7_segment_display_1 (
    .g(or_9_out), .f(or_10_out), .a(or_11_out), .b(or_12_out), .e(or_8_out), .d(or_7_out), .c(or_13_out));  // open: dp

  // Notes on the sheet:
  //   B
  //   D
  //   C
  //   E
  //   C
  //   D
  //   E
endmodule
